# Fritzing sketch 28byj-48-step-motor (saved by Fritzing 1.0.3b)

parts:
  Part1 = Arduino Mega 2560 (Rev3)
  Driver1 = 28byj-48-driver_roboteach_es_1 [part_number=ULN2003]
  SM1 = 28BYJ-48 Stepper Motor [part_number=28BYJ-48]

nets:
  N1: Part1.D11_PWM, Driver1.connector0
  N2: Part1.D10_PWM, Driver1.connector1
  N3: Part1.D9_PWM, Driver1.connector2
  N4: Part1.D8_PWM, Driver1.connector3
  N5: Part1.5V, Driver1.connector5
  N6: Part1.GND, Driver1.connector4
  N7: Driver1.connector8, SM1.blue-pin
  N8: Driver1.connector9, SM1.pink-pin
  N9: Driver1.connector10, SM1.yellow-pin
  N10: Driver1.connector11, SM1.orange-pin
  N11: Driver1.connector12, SM1.red-pin

custom parts:
  28BYJ-48 Stepper Motor: Unipolar Stepper Motor 28BYJ-48 Top coil - pink & orange Bottom coil - blue & yellow Common rail - red Connector pins: blue - pink - yellow - orange - red
