# Fritzing sketch night-light (saved by Fritzing 1.0.3b)
breadboards: 1

parts:
  Part1 = Arduino Mega 2560 (Rev3)
  R1 = PHOTOCELL [package=photocell-kit]
  R2 = Resistor [tolerance=±5% power=0.25W resistance=220 package=THT]
  LED2 = LED - 5mm [color="Red (633nm)" current=0.030A package="5 mm [THT]"]
  R3 = Resistor [tolerance=±5% power=0.25W resistance=220 package=THT]

nets:
  N1: Part1.A0, R1.P$2, R2.Pin_1
  N2: Part1.5V, R1.P$1
  N3: Part1.GND, R2.Pin_0, R3.Pin_0
  N4: Part1.D7_PWM, LED2.cathode
  N5: LED2.anode, R3.Pin_1
