# Fritzing sketch sound-sensor (saved by Fritzing 1.0.3b)
breadboards: 1

parts:
  FC-1 = Sound Sensor
  Part1 = Arduino Mega 2560 (Rev3)
  LED2 = LED - 5mm [color="Red (633nm)" current=0.030A package="5 mm [THT]"]
  R1 = Rotary Potentiometer (Small) [maximum_resistance=10kΩ knob_status=50% power=0.5W package=THT]
  LCD1 = LCD screen
  R5 = Resistor [tolerance=±5% power=0.25W resistance=220 package=THT]

nets:
  VCC: FC-1.VCC, Part1.5V, R1.leg2, LCD1.VDD, LCD1.LED+
  GND: FC-1.GND, R1.leg1, LCD1.VSS, LCD1.LED-, R5.Pin_1
  N1: FC-1.OUT, Part1.A1
  N2: Part1.D13_PWM, LCD1.RS
  N3: Part1.D12_PWM, LCD1.E
  N4: Part1.D11_PWM, LCD1.DB4
  N5: Part1.D10_PWM, LCD1.DB5
  N6: Part1.D8_PWM, LCD1.DB7
  N7: Part1.D3_PWM, LED2.cathode
  N8: LED2.anode, R5.Pin_0
  N9: R1.wiper, LCD1.V0
